# Fritzing sketch TelegramBot (saved by Fritzing 0.9.3b)

parts:
  Raspberry_Pi_1 = Raspberry Pi 3 [part_number=RPI-3-V1.2]
  RHT1 = Humidity and Temperature Sensor RHT03
  Part1 = Arduino Nano (Rev3.0)  # not connected

nets:
  3V3: Raspberry_Pi_1.3v3, RHT1.Vcc
  N1: Raspberry_Pi_1.GPIO4, RHT1.GND_2
  N2: Raspberry_Pi_1.GND, RHT1.Data-signal, RHT1.GND_1
