# Fritzing sketch TelegramBot_raspberry_pi_version (saved by Fritzing 0.9.3b)

parts:
  Raspberry_Pi_1 = Raspberry Pi 3 [part_number=RPI-3-V1.2]
  RHT1 = Humidity and Temperature Sensor RHT03
  S3 = Pushbutton [package=THT]
  S4 = Pushbutton [package=THT]
  S5 = Pushbutton [package=THT]

nets:
  3V3: Raspberry_Pi_1.3v3, Raspberry_Pi_1.3V3, RHT1.Vcc, S5.leg0
  N1: Raspberry_Pi_1.GPIO4, RHT1.GND_2
  N2: Raspberry_Pi_1.GND, RHT1.Data-signal, RHT1.GND_1
  N3: Raspberry_Pi_1.GPIO24, S5.leg1
  N4: Raspberry_Pi_1.GPIO23, S4.leg0
  N5: Raspberry_Pi_1.GPIO18, S3.leg0
  N6: Raspberry_Pi_1.5V, S3.leg1, S4.leg1

notes:
  Buttons
